# Fritzing sketch FinalSystem (saved by Fritzing 1.0.4)

parts:
  Part1 = Arduino Uno (Rev3)
  Part2 = Thumb Joystick
  J2 = Basic Servo
  VCC1 = 4 x AAA Battery Mount [internal_resistance=0.1Ω]  # not connected
  J1 = Basic Servo
  Part3 = Arduino Mega 2560 (Rev3)
  U1 = ESP32-38PinWide [part_number=ESP32-38PinWide]
  U2 = ESP32-38PinWide [part_number=ESP32-38PinWide]
  Part4 = I2C level shifter bidirectional
  Part5 = I2C level shifter bidirectional

nets:
  N1: Part1.D9_PWM, J1.pulse
  N2: Part1.D10_PWM/SS, J2.pulse
  N3: Part1.D0/RX, Part4.HV1
  5V: Part1.5V, U2.VIN
  N4: Part1.GND, U2.GPIO11
  GND: Part2.GND, Part3.GND, U1.GPIO11
  N5: Part2.HORZ, Part3.A1
  N6: Part2.VERT, Part3.A0
  VCC: Part2.VCC, Part3.5V, U1.VIN
  N7: Part3.D18/TX1, Part5.LV1
  N8: U1.GPIO3, Part5.HV1
  N9: U2.GPIO1, Part4.LV1

custom parts:
  ESP32-38PinWide: Generic 38-Pin ESP32 with wide format (only access to one side of pins on a breadboard) based on Stephen Lilley's HiLetgo ESP-WROOM-32 ESP32 ESP-32S Development Board.
