# Fritzing sketch JoystickServo2 (saved by Fritzing 1.0.4)

parts:
  Part1 = Arduino Uno (Rev3)
  Part2 = Thumb Joystick
  J2 = Basic Servo
  VCC1 = 4 x AAA Battery Mount [internal_resistance=0.1Ω]  # not connected
  J1 = Basic Servo

nets:
  N1: Part1.A0, Part2.VERT
  N2: Part1.A1, Part2.HORZ
  N3: Part1.D9_PWM, J1.pulse
  N4: Part1.D10_PWM/SS, J2.pulse
  N5: Part1.D2, Part2.SEL
  5V: Part1.5V, Part2.VCC
  GND: Part1.GND, Part2.GND
