# Fritzing sketch SimpleJoystick (saved by Fritzing 1.0.4)
breadboards: 1

parts:
  Part1 = Arduino Uno (Rev3)
  Part2 = Thumb Joystick
  LED1 = LED - 5mm [color="Red (633nm)" current=0.030A package="5 mm [THT]"]
  LED2 = LED - 5mm [color="Red (633nm)" current=0.030A package="5 mm [THT]"]
  LED4 = LED - 5mm [color="Red (633nm)" current=0.030A package="5 mm [THT]"]
  LED3 = LED - 5mm [color="Red (633nm)" current=0.030A package="5 mm [THT]"]

nets:
  N1: Part1.A0, Part2.HORZ
  N2: Part1.A1, Part2.SEL
  N3: Part1.D9_PWM, LED1.anode
  N4: Part1.D2, Part2.VERT
  N5: Part1.D3_PWM, LED4.anode
  N6: Part1.D5_PWM, LED3.anode
  N7: Part1.D6_PWM, LED2.anode
  5V: Part1.5V, Part2.VCC
  GND: Part1.GND, Part2.GND, LED1.cathode, LED2.cathode, LED4.cathode, LED3.cathode
